// Logisim project 10.1.circ as structural Verilog: 1 circuit, main circuit main
module main (
  input  in_1,
  input  in_2,
  input  in_3,
  input  a,
  input  b,
  input  c,
  output out_7,
  output S
);

  wire and_1_out, and_2_out, and_3_out, not_1_out, not_2_out, not_3_out, not_4_out, not_5_out, not_6_out;

  not not_1 (not_1_out, b);
  not not_2 (not_2_out, c);
  not not_3 (not_3_out, a);
  not not_4 (not_4_out, c);
  not not_5 (not_5_out, a);
  not not_6 (not_6_out, b);
  ExactlyOne xor_1 (.out(out_7), .in0(in_1), .in1(in_2), .in2(in_3));
  and and_1 (and_1_out, a, not_1_out, not_2_out);
  and and_2 (and_2_out, not_3_out, b, not_4_out);
  and and_3 (and_3_out, not_5_out, not_6_out, c);
  or or_1 (S, and_1_out, and_2_out, and_3_out);
endmodule
