// Logisim project 10.4non_fini.circ as structural Verilog: 1 circuit, main circuit main
module main (
  input  in_1,
  input  in_2,
  input  in_3,
  input  in_4,
  input  in_5
);

  wire and_1_out, and_2_out, not_1_out, not_2_out, not_3_out, or_3_out;

  not not_1 (not_1_out, in_1);
  not not_2 (not_2_out, in_2);
  not not_3 (not_3_out, in_3);
  // OR_Gate or_1 has open pins: in0=not_3_out, in1=in_4, out=open
  // OR_Gate or_2 is placed but not wired
  and and_1 (and_1_out, in_1, not_2_out);
  and and_2 (and_2_out, not_1_out, in_2);
  // AND_Gate and_3 is placed but not wired
  or or_3 (or_3_out, and_1_out, and_2_out);

  assign in_5 = in_4;
endmodule
