// Logisim project recap.circ as structural Verilog: 7 circuits, main circuit main
module main (
  input  in_1
);
endmodule

module mux (
  input  c,
  input  a,
  input  b,
  output S
);

  wire and_1_out, and_2_out, not_1_out;

  not not_1 (not_1_out, c);
  and and_1 (and_1_out, a, not_1_out);
  and and_2 (and_2_out, b, c);
  or or_1 (S, and_1_out, and_2_out);
endmodule

module Inv (
  input  c,
  input  a,
  output S
);

  wire and_1_out, and_2_out, not_1_out, not_2_out;

  not not_1 (not_1_out, c);
  not not_2 (not_2_out, a);
  and and_1 (and_1_out, a, not_1_out);
  and and_2 (and_2_out, not_2_out, c);
  or or_1 (S, and_1_out, and_2_out);
endmodule

module Mux1parmi4 (
  input  c0,
  input  c1,
  input  in_3,
  input  in_4,
  input  in_5,
  input  in_6,
  output S
);

  wire mux_1_s, mux_2_s;

  mux mux_1 (.c(c0), .a(in_3), .b(in_4), .S(mux_1_s));
  mux mux_2 (.c(c0), .a(in_5), .b(in_6), .S(mux_2_s));
  mux mux_3 (.c(c1), .a(mux_1_s), .b(mux_2_s), .S(S));
endmodule

module Mux1parmi8 (
  input  in_1,
  input  in_2,
  input  in_3,
  input  in_4,
  input  in_5,
  input  in_6,
  input  in_7,
  input  in_8,
  input  in_9,
  input  in_10,
  input  in_11
);

  wire mux_1_s, mux_2_s, mux_3_s, mux_4_s, mux_5_s, mux_6_s;

  mux mux_1 (.c(in_1), .a(in_4), .b(in_5), .S(mux_1_s));
  mux mux_2 (.c(in_1), .a(in_6), .b(in_7), .S(mux_2_s));
  mux mux_3 (.c(in_1), .a(in_8), .b(in_9), .S(mux_3_s));
  mux mux_4 (.c(in_1), .a(in_10), .b(in_11), .S(mux_4_s));
  mux mux_5 (.c(in_2), .a(mux_1_s), .b(mux_2_s), .S(mux_5_s));
  mux mux_6 (.c(in_2), .a(mux_3_s), .b(mux_4_s), .S(mux_6_s));
  mux mux_7 (.c(in_3), .a(mux_5_s), .b(mux_6_s));  // open: S
endmodule

module Alu1bit (
  input  in_1,
  input  in_2,
  input  in_3,
  input  in_4,
  input  in_5,
  input  in_6,
  output S,
  output r_out
);

  wire addsub1bit_1_s, and_1_out, not_1_out, or_1_out;

  not not_1 (not_1_out, in_5);
  and and_1 (and_1_out, in_5, in_6);
  or or_1 (or_1_out, in_5, in_6);
  AddSub1bit addsub1bit_1 (.c(in_2), .r_in(in_1), .in_3(in_5), .in_4(in_6), .S(addsub1bit_1_s), .r_out(r_out));
  Mux1parmi4 mux1parmi4_1 (
    .c0(in_4), .c1(in_3), .in_3(not_1_out), .in_4(addsub1bit_1_s), .in_5(and_1_out), .in_6(or_1_out), .S(S));
endmodule

module AddSub1bit (
  input  c,
  input  r_in,
  input  in_3,
  input  in_4,
  output S,
  output r_out
);

  wire and_1_out, and_2_out, and_3_out, inv_1_s, xor_1_out;

  Inv inv_1 (.c(c), .a(in_4), .S(inv_1_s));
  xor xor_1 (xor_1_out, in_3, inv_1_s);
  and and_1 (and_1_out, in_3, r_in);
  and and_2 (and_2_out, inv_1_s, r_in);
  and and_3 (and_3_out, in_3, inv_1_s);
  xor xor_2 (S, xor_1_out, r_in);
  or or_1 (r_out, and_1_out, and_2_out, and_3_out);
endmodule
