// Logisim project 10.2.circ as structural Verilog: 1 circuit, main circuit main
module main (
  input  [3:0] in_1,
  output out_2
);

  wire and_1_out, and_2_out;

  and and_1 (and_1_out, in_1[1], in_1[3]);
  and and_2 (and_2_out, in_1[3], in_1[2]);
  or or_1 (out_2, and_1_out, and_2_out);

  // Notes on the sheet:
  //   Raisonnement: 
  //   Splitter les bits: abcd
  //   Dresser Table vérité
  //   Dresser Tableau Karnaug
  //   Définir fonciton simplifiée 
  //   Realiser le circuit
  //   f(a,b,c,d) = ab + ac
endmodule
