// Logisim project 6.14.circ as structural Verilog
module Add1bit (
  input  A,
  input  B,
  input  C,
  output S,
  output R
);

  wire and_1_out, and_2_out, and_3_out, xor_1_out;

  xor xor_1 (xor_1_out, A, B);
  and and_1 (and_1_out, A, B);
  and and_2 (and_2_out, A, C);
  and and_3 (and_3_out, B, C);
  xor xor_2 (S, xor_1_out, C);
  or or_1 (R, and_1_out, and_2_out, and_3_out);

  // Notes on the sheet:
  //   retenue
  //   nb1
  //   nb2
  //   S = (A+!B) +! C
  //   (A~B + ~AB) +! C
endmodule

module Add4bit (
  input  in_1,
  input  [3:0] in_2,
  input  [3:0] in_3,
  output [3:0] out_4,
  output out_5
);

  wire add1bit_1_r, add1bit_2_r, add1bit_3_r;

  Add1bit add1bit_1 (.A(in_2[0]), .B(in_3[0]), .C(in_1), .S(out_4[0]), .R(add1bit_1_r));
  Add1bit add1bit_2 (.A(in_2[1]), .B(in_3[1]), .C(add1bit_1_r), .S(out_4[1]), .R(add1bit_2_r));
  Add1bit add1bit_3 (.A(in_2[2]), .B(in_3[2]), .C(add1bit_2_r), .S(out_4[2]), .R(add1bit_3_r));
  Add1bit add1bit_4 (.A(in_2[3]), .B(in_3[3]), .C(add1bit_3_r), .S(out_4[3]), .R(out_5));
endmodule

module Sub4bit (
  input  r,
  input  [3:0] nb1,
  input  [3:0] nb2,
  output [3:0] S
);

  wire add1bit_1_r, add1bit_2_r, add1bit_3_r, not_1_out, not_2_out, not_3_out, not_4_out;

  not not_1 (not_1_out, nb2[0]);
  not not_2 (not_2_out, nb2[1]);
  not not_3 (not_3_out, nb2[2]);
  not not_4 (not_4_out, nb2[3]);
  Add1bit add1bit_1 (.A(nb1[0]), .B(not_1_out), .C(r), .S(S[0]), .R(add1bit_1_r));
  Add1bit add1bit_2 (.A(nb1[1]), .B(not_2_out), .C(add1bit_1_r), .S(S[1]), .R(add1bit_2_r));
  Add1bit add1bit_3 (.A(nb1[2]), .B(not_3_out), .C(add1bit_2_r), .S(S[2]), .R(add1bit_3_r));
  Add1bit add1bit_4 (.A(nb1[3]), .B(not_4_out), .C(add1bit_3_r), .S(S[3]));  // open: R

  // Notes on the sheet:
  //   Les nombres sonten CA2
  //   * on ajoute 1
  //      * on calcul le CA1 du nombre a soustraire 
  //   nb1
  //   Logique:
  //   a - b = a + CA2(b)
  //   a - b = a + (CA1(b) + 1)
  //   a - b = a + 1 + CA1(b)
  //   a - b = a + CA1(b) + 1
  //   nb2
  //   (bits inversés)
  //   r = 1
endmodule

module Inv (
  input  C,
  input  A,
  output S
);

  wire and_1_out, and_2_out, not_1_out, not_2_out;

  not not_1 (not_1_out, C);
  not not_2 (not_2_out, A);
  and and_1 (and_1_out, A, not_1_out);
  and and_2 (and_2_out, C, not_2_out);
  or or_1 (S, and_1_out, and_2_out);
endmodule

module AddSub4bit (
  input  c,
  input  [3:0] nb1,
  input  [3:0] nb2,
  output [3:0] s,
  output r
);

  wire add1bit_1_r, add1bit_2_r, add1bit_3_r, inv_1_s, inv_2_s, inv_3_s, inv_4_s;

  Inv inv_1 (.C(c), .A(nb2[0]), .S(inv_1_s));
  Inv inv_2 (.C(c), .A(nb2[1]), .S(inv_2_s));
  Inv inv_3 (.C(c), .A(nb2[2]), .S(inv_3_s));
  Inv inv_4 (.C(c), .A(nb2[3]), .S(inv_4_s));
  Add1bit add1bit_1 (.A(nb1[0]), .B(inv_1_s), .C(c), .S(s[0]), .R(add1bit_1_r));
  Add1bit add1bit_2 (.A(nb1[1]), .B(inv_2_s), .C(add1bit_1_r), .S(s[1]), .R(add1bit_2_r));
  Add1bit add1bit_3 (.A(nb1[2]), .B(inv_3_s), .C(add1bit_2_r), .S(s[2]), .R(add1bit_3_r));
  Add1bit add1bit_4 (.A(nb1[3]), .B(inv_4_s), .C(add1bit_3_r), .S(s[3]), .R(r));

  // Notes on the sheet:
  //   l'inversion se fait
  //   grace à 
  //   des inverseur
  //   Additionneur : si c = 0
  //   Soustracteur si c = 1
  //   c est donné à la retenue du premier ADD1bit
endmodule

module Mux (
  input  c,
  input  a,
  input  b,
  output S
);

  wire and_1_out, and_2_out, not_1_out;

  not not_1 (not_1_out, c);
  and and_1 (and_1_out, a, not_1_out);
  and and_2 (and_2_out, b, c);
  or or_1 (S, and_1_out, and_2_out);
endmodule

module ALU1bit (
  input  r_in,
  input  c0,
  input  c1,
  input  c2,
  input  a,
  input  b,
  input  r_out,
  output out_8
);

  wire addsub1bit_1_s, and_1_out, not_1_out, or_1_out;

  not not_1 (not_1_out, a);
  AddSub1bit addsub1bit_1 (.r_in(r_in), .c(c0), .a(a), .b(b), .S(addsub1bit_1_s), .r(r_out));
  or or_1 (or_1_out, a, b);
  and and_1 (and_1_out, a, b);
  Mux1parmi4 mux1parmi4_1 (
    .c0(c2), .c1(c1), .nb1(not_1_out), .nb2(addsub1bit_1_s), .nb3(or_1_out), .nb4(and_1_out), .S(out_8));
endmodule

module Mux1parmi4 (
  input  c0,
  input  c1,
  input  nb1,
  input  nb2,
  input  nb3,
  input  nb4,
  output S
);

  wire mux_1_s, mux_2_s;

  Mux mux_1 (.c(c0), .a(nb1), .b(nb2), .S(mux_1_s));
  Mux mux_2 (.c(c0), .a(nb3), .b(nb4), .S(mux_2_s));
  Mux mux_3 (.c(c1), .a(mux_1_s), .b(mux_2_s), .S(S));

  // Notes on the sheet:
  //   00 = a
  //   01 = c
  //   10 = b
  //   11 = d
endmodule

module Mux1parmi8 (
  input  c0,
  input  c1,
  input  c2,
  input  n1,
  input  n2,
  input  n3,
  input  n4,
  input  n5,
  input  n6,
  input  n7,
  input  n8,
  output S
);

  wire mux_1_s, mux_2_s, mux_3_s, mux_4_s, mux_5_s, mux_6_s;

  Mux mux_1 (.c(c0), .a(n1), .b(n2), .S(mux_1_s));
  Mux mux_2 (.c(c0), .a(n3), .b(n4), .S(mux_2_s));
  Mux mux_3 (.c(c0), .a(n5), .b(n6), .S(mux_3_s));
  Mux mux_4 (.c(c0), .a(n7), .b(n8), .S(mux_4_s));
  Mux mux_5 (.c(c1), .a(mux_1_s), .b(mux_2_s), .S(mux_5_s));
  Mux mux_6 (.c(c1), .a(mux_3_s), .b(mux_4_s), .S(mux_6_s));
  Mux mux_7 (.c(c2), .a(mux_5_s), .b(mux_6_s), .S(S));

  // Notes on the sheet:
  //   000 = n1
  //   001 = n5
  //   010 = n3
  //   011 = n7
  //   100 = n2
  //   101 = n6
  //   110 = n4
  //   111 = n8
endmodule

module AddSub1bit (
  input  r_in,
  input  c,
  input  a,
  input  b,
  output S,
  output r
);

  wire inv_1_s;

  Inv inv_1 (.C(r_in), .A(b), .S(inv_1_s));
  Add1bit add1bit_1 (.A(a), .B(inv_1_s), .C(c), .S(S), .R(r));
endmodule

module Mux1parmi5 (
  input  c0,
  input  c1,
  input  c2,
  input  n1,
  input  n2,
  input  n3,
  input  n4,
  input  n5,
  output out_9
);

  wire mux_1_s, mux_2_s, mux_3_s;

  Mux mux_1 (.c(c0), .a(n1), .b(n2), .S(mux_1_s));
  Mux mux_2 (.c(c0), .a(n3), .b(n4), .S(mux_2_s));
  Mux mux_3 (.c(c1), .a(mux_1_s), .b(mux_2_s), .S(mux_3_s));
  Mux mux_4 (.c(c2), .a(mux_3_s), .b(n5), .S(out_9));

  // Notes on the sheet:
  //   000 = a
  //   001 = c
  //   010 = b
  //   011 = d
  //   100 = 5
  //   101 = 5
  //   110 = 5
  //   111 = 5
endmodule

module Mux1parmi32 (
  input  c0,
  input  c1,
  input  c2,
  input  c3,
  input  c4,
  input  n1,
  input  n2,
  input  n3,
  input  n4,
  input  n5,
  input  n6,
  input  n7,
  input  n8,
  input  n9,
  input  n10,
  input  n11,
  input  n12,
  input  n13,
  input  n14,
  input  n15,
  input  n16,
  input  n17,
  input  n18,
  input  n19,
  input  n20,
  input  n21,
  input  n22,
  input  n23,
  input  n24,
  input  n25,
  input  n26,
  input  n27,
  input  n28,
  input  n29,
  input  n30,
  input  n31,
  input  n32,
  output S
);

  wire mux1parmi8_1_s, mux1parmi8_2_s, mux1parmi8_3_s, mux1parmi8_4_s;

  Mux1parmi8 mux1parmi8_1 (
    .c0(c0), .c1(c1), .c2(c2), .n1(n1), .n2(n2), .n3(n3), .n4(n4), .n5(n5), .n6(n6), .n7(n7), .n8(n8),
    .S(mux1parmi8_1_s));
  Mux1parmi8 mux1parmi8_2 (
    .c0(c0), .c1(c1), .c2(c2), .n1(n9), .n2(n10), .n3(n11), .n4(n12), .n5(n13), .n6(n14), .n7(n15), .n8(n16),
    .S(mux1parmi8_2_s));
  Mux1parmi8 mux1parmi8_3 (
    .c0(c0), .c1(c1), .c2(c2), .n1(n17), .n2(n18), .n3(n19), .n4(n20), .n5(n21), .n6(n22), .n7(n23),
    .n8(n24), .S(mux1parmi8_3_s));
  Mux1parmi8 mux1parmi8_4 (
    .c0(c0), .c1(c1), .c2(c2), .n1(n25), .n2(n26), .n3(n27), .n4(n28), .n5(n29), .n6(n30), .n7(n31),
    .n8(n32), .S(mux1parmi8_4_s));
  Mux1parmi4 mux1parmi4_1 (
    .c0(c4), .c1(c3), .nb1(mux1parmi8_1_s), .nb2(mux1parmi8_2_s), .nb3(mux1parmi8_3_s), .nb4(mux1parmi8_4_s),
    .S(S));
endmodule

module Mux1parmi64 (
  input  c0,
  input  c1,
  input  c2,
  input  c3,
  input  c4,
  input  c5,
  input  n1,
  input  n2,
  input  n3,
  input  n4,
  input  n5,
  input  n6,
  input  n7,
  input  n8,
  input  n9,
  input  n10,
  input  n11,
  input  n12,
  input  n13,
  input  n14,
  input  n15,
  input  n16,
  input  n17,
  input  n18,
  input  n19,
  input  n20,
  input  n21,
  input  n22,
  input  n23,
  input  n24,
  input  n25,
  input  n26,
  input  n27,
  input  n28,
  input  n29,
  input  n30,
  input  n31,
  input  n32,
  input  n33,
  input  n34,
  input  n35,
  input  n36,
  input  n37,
  input  n38,
  input  n39,
  input  n40,
  input  n41,
  input  n42,
  input  n43,
  input  n44,
  input  n45,
  input  n46,
  input  n47,
  input  n48,
  input  n49,
  input  n50,
  input  n51,
  input  n52,
  input  n53,
  input  n54,
  input  n55,
  input  n56,
  input  n57,
  input  n58,
  input  n59,
  input  n60,
  input  n61,
  input  n62,
  input  n63,
  input  n64,
  output S
);

  wire mux1parmi32_1_s, mux1parmi32_2_s;

  Mux1parmi32 mux1parmi32_1 (
    .c0(c0), .c1(c1), .c2(c2), .c3(c3), .c4(c4), .n1(n1), .n2(n2), .n3(n3), .n4(n4), .n5(n5), .n6(n6),
    .n7(n7), .n8(n8), .n9(n9), .n10(n10), .n11(n11), .n12(n12), .n13(n13), .n14(n14), .n15(n15), .n16(n16),
    .n17(n17), .n18(n18), .n19(n19), .n20(n20), .n21(n21), .n22(n22), .n23(n23), .n24(n24), .n25(n25),
    .n26(n26), .n27(n27), .n28(n28), .n29(n29), .n30(n30), .n31(n31), .n32(n32), .S(mux1parmi32_1_s));
  Mux1parmi32 mux1parmi32_2 (
    .c0(c0), .c1(c1), .c2(c2), .c3(c3), .c4(c4), .n1(n33), .n2(n34), .n3(n35), .n4(n36), .n5(n37), .n6(n38),
    .n7(n39), .n8(n40), .n9(n41), .n10(n42), .n11(n43), .n12(n44), .n13(n45), .n14(n46), .n15(n47),
    .n16(n48), .n17(n49), .n18(n50), .n19(n51), .n20(n52), .n21(n53), .n22(n54), .n23(n55), .n24(n56),
    .n25(n57), .n26(n58), .n27(n59), .n28(n60), .n29(n61), .n30(n62), .n31(n63), .n32(n64),
    .S(mux1parmi32_2_s));
  Mux mux_1 (.c(c5), .a(mux1parmi32_1_s), .b(mux1parmi32_2_s), .S(S));
endmodule

module DecodeurElementaire (
  input  a,
  output s0,
  output s1
);

  not not_1 (s0, a);

  assign s1 = a;
endmodule
