// Logisim project exercice_6.7.circ as structural Verilog: 1 circuit, main circuit main
module main (
  input  e1,
  input  e2,
  input  e3,
  input  a,
  input  b,
  input  c,
  output S1,
  output S
);

  wire and_1_out, and_2_out, and_3_out, not_1_out, not_2_out, not_3_out, not_4_out, not_5_out, not_6_out;

  not not_1 (not_1_out, b);
  not not_2 (not_2_out, c);
  not not_3 (not_3_out, a);
  not not_4 (not_4_out, c);
  not not_5 (not_5_out, a);
  not not_6 (not_6_out, b);
  ExactlyOne xor_1 (.out(S1), .in0(e1), .in1(e2), .in2(e3));
  and and_1 (and_1_out, a, not_1_out, not_2_out);
  and and_2 (and_2_out, not_3_out, b, not_4_out);
  and and_3 (and_3_out, not_5_out, not_6_out, c);
  or or_1 (S, and_1_out, and_2_out, and_3_out);

  // Notes on the sheet:
  //   EXERCICE 6.7 : schématiser la fonction OU(exclusif)
endmodule
