// Logisim project exercice_6.8.circ as structural Verilog: 1 circuit, main circuit main
module main (
  input  [3:0] in_1,
  output out_2
);

  wire and_1_out, and_2_out;

  and and_1 (and_1_out, in_1[1], in_1[3]);
  and and_2 (and_2_out, in_1[3], in_1[2]);
  or or_1 (out_2, and_1_out, and_2_out);

  // Notes on the sheet:
  //   Exercice 6.8 : Circuit renvoyant 1 pour tout nombres >= 10 
endmodule
