// Logisim project exercice_6.9.circ as structural Verilog: 1 circuit, main circuit main
module main (
  input  [3:0] in_1,
  output S
);

  wire and_1_out, and_2_out, and_3_out, and_4_out, and_5_out, not_1_out, not_2_out, not_3_out, not_4_out;

  not not_1 (not_1_out, in_1[0]);
  not not_2 (not_2_out, in_1[1]);
  not not_3 (not_3_out, in_1[2]);
  not not_4 (not_4_out, in_1[3]);
  and and_1 (and_1_out, in_1[3], in_1[2], not_2_out, not_1_out);
  and and_2 (and_2_out, in_1[3], not_3_out, not_2_out, in_1[0]);
  and and_3 (and_3_out, not_4_out, in_1[2], in_1[1], not_1_out);
  or or_1 (S, and_1_out, and_2_out, and_3_out, and_4_out, and_5_out);
  and and_4 (and_4_out, not_4_out, not_3_out, in_1[1], in_1[0]);
  and and_5 (and_5_out, in_1[3], in_1[2], in_1[1], in_1[0]);

  // Notes on the sheet:
  //   EXERCICE 6.9 : Realiser un circuit qui recoit un nombre codé sur 4 bits et renvoi 1 si ce nombre est divisible par 3
  //   a
  //   b
  //   c
  //   d
  //   ~a
  //   ~b
  //   ~c
  //   ~d
endmodule
