// Logisim project exo6.3.circ as structural Verilog: 1 circuit, main circuit main
module main (
  input  a,
  input  b,
  output a_OU_exclusif__b
);

  wire transistor_1_out, transistor_3_out, transistor_6_out, transistor_8_out;

  Transistor transistor_1 (.in(1'b1), .out(transistor_1_out), .gate(a));
  Transistor #(.\type ("n")) transistor_2 (.in(transistor_1_out), .out(a_OU_exclusif__b), .gate(b));
  Transistor #(.\type ("n")) transistor_3 (.in(1'b1), .out(transistor_3_out), .gate(a));
  Transistor transistor_4 (.in(transistor_3_out), .out(a_OU_exclusif__b), .gate(b));
  Transistor #(.\type ("n")) transistor_5 (.in(transistor_6_out), .out(a_OU_exclusif__b), .gate(a));
  Transistor #(.\type ("n")) transistor_6 (.in(1'b0), .out(transistor_6_out), .gate(b));
  Transistor transistor_7 (.in(transistor_8_out), .out(a_OU_exclusif__b), .gate(a));
  Transistor transistor_8 (.in(1'b0), .out(transistor_8_out), .gate(b));
endmodule
