// Logisim project exo6.5.circ as structural Verilog: 1 circuit, main circuit main
module main (
  input  a,
  input  b,
  output n_a___b
);

  wire transistor_2_out;

  Transistor #(.\type ("n")) transistor_1 (.in(1'b0), .out(n_a___b), .gate(a));
  Transistor transistor_2 (.in(1'b1), .out(transistor_2_out), .gate(a));
  Transistor transistor_3 (.in(transistor_2_out), .out(n_a___b), .gate(b));
  Transistor #(.\type ("n")) transistor_4 (.in(1'b0), .out(n_a___b), .gate(b));
endmodule
