// Logisim project exercices7.circ as structural Verilog
module BasculeRS (
  input  R,
  input  S,
  output Q
);

  wire nor_2_out;

  nor nor_1 (Q, R, nor_2_out);
  nor nor_2 (nor_2_out, Q, S);
endmodule

module BasculeD (
  input  D,
  input  data_in,
  output q
);

  wire and_1_out, and_2_out, nor_2_out, not_1_out;

  not not_1 (not_1_out, data_in);
  and and_1 (and_1_out, not_1_out, D);
  and and_2 (and_2_out, D, data_in);
  nor nor_1 (q, and_1_out, nor_2_out);
  nor nor_2 (nor_2_out, q, and_2_out);
endmodule

module Lecture (
  input  a1,
  input  a2,
  output data_out
);

  wire and_1_out, and_2_out, and_3_out, and_4_out, and_5_out, and_6_out, and_7_out, and_8_out, basculed_1_q,
       basculed_2_q, basculed_3_q, basculed_4_q, not_1_out, not_2_out, not_3_out, not_4_out, or_1_out,
       or_3_out, undriven, undriven_2, undriven_3, undriven_4;

  not not_1 (not_1_out, a1);
  not not_2 (not_2_out, a2);
  and and_1 (and_1_out, not_2_out, not_1_out);
  BasculeD basculed_1 (.D(undriven), .q(basculed_1_q));  // open: data_in
  not not_3 (not_3_out, a2);
  and and_2 (and_2_out, not_3_out, a1);
  and and_3 (and_3_out, a2, not_4_out);
  BasculeD basculed_2 (.D(undriven_2), .q(basculed_2_q));  // open: data_in
  not not_4 (not_4_out, a1);
  BasculeD basculed_3 (.D(undriven_3), .q(basculed_3_q));  // open: data_in
  and and_4 (and_4_out, a2, a1);
  BasculeD basculed_4 (.D(undriven_4), .q(basculed_4_q));  // open: data_in
  or or_1 (or_1_out, and_5_out, and_6_out);
  and and_5 (and_5_out, and_4_out, basculed_4_q);
  or or_2 (data_out, or_1_out, or_3_out);
  and and_6 (and_6_out, and_3_out, basculed_3_q);
  and and_7 (and_7_out, and_2_out, basculed_2_q);
  or or_3 (or_3_out, and_7_out, and_8_out);
  and and_8 (and_8_out, and_1_out, basculed_1_q);
endmodule

module Lecture_Ecriture (
  input  a1,
  input  a2,
  input  nonLire_ecrire,
  input  data_in,
  output data_out
);

  wire and_1_out, and_2_out, and_3_out, and_4_out, and_5_out, and_6_out, and_7_out, and_8_out, and_9_out,
       and_10_out, and_11_out, and_13_out, basculed_1_q, basculed_2_q, basculed_3_q, basculed_4_q, not_1_out,
       not_2_out, not_3_out, not_4_out, not_5_out, or_1_out, or_2_out, or_3_out;

  not not_1 (not_1_out, a1);
  not not_2 (not_2_out, a2);
  and and_1 (and_1_out, not_2_out, not_1_out);
  and and_2 (and_2_out, nonLire_ecrire, and_1_out);
  not not_3 (not_3_out, a2);
  and and_3 (and_3_out, not_3_out, a1);
  and and_4 (and_4_out, nonLire_ecrire, and_3_out);
  and and_5 (and_5_out, a2, not_4_out);
  and and_6 (and_6_out, nonLire_ecrire, and_5_out);
  not not_4 (not_4_out, a1);
  and and_7 (and_7_out, nonLire_ecrire, and_8_out);
  BasculeD basculed_1 (.D(and_2_out), .data_in(data_in), .q(basculed_1_q));
  and and_8 (and_8_out, a2, a1);
  BasculeD basculed_2 (.D(and_4_out), .data_in(data_in), .q(basculed_2_q));
  BasculeD basculed_3 (.D(and_6_out), .data_in(data_in), .q(basculed_3_q));
  BasculeD basculed_4 (.D(and_7_out), .data_in(data_in), .q(basculed_4_q));
  and and_9 (and_9_out, and_8_out, basculed_4_q);
  not not_5 (not_5_out, nonLire_ecrire);
  or or_1 (or_1_out, and_9_out, and_10_out);
  and and_10 (and_10_out, and_5_out, basculed_3_q);
  or or_2 (or_2_out, or_1_out, or_3_out);
  and and_11 (and_11_out, and_3_out, basculed_2_q);
  and and_12 (data_out, not_5_out, or_2_out);
  or or_3 (or_3_out, and_11_out, and_13_out);
  and and_13 (and_13_out, and_1_out, basculed_1_q);
endmodule

module Memory_2x2bits (
  input  a,
  input  nonlire_ecrire,
  input  data_in_1,
  input  data_in_2,
  output data_out_1,
  output data_out_2
);

  wire and_1_out, and_2_out, and_3_out, and_4_out, and_7_out, and_8_out, basculed_1_q, basculed_2_q,
       basculed_3_q, basculed_4_q, not_1_out, not_2_out, or_1_out, or_2_out;

  not not_1 (not_1_out, a);
  and and_1 (and_1_out, nonlire_ecrire, not_1_out);
  and and_2 (and_2_out, nonlire_ecrire, a);
  BasculeD basculed_1 (.D(and_1_out), .data_in(data_in_1), .q(basculed_1_q));
  BasculeD basculed_2 (.D(and_1_out), .data_in(data_in_2), .q(basculed_2_q));
  not not_2 (not_2_out, nonlire_ecrire);
  BasculeD basculed_3 (.D(and_2_out), .data_in(data_in_1), .q(basculed_3_q));
  BasculeD basculed_4 (.D(and_2_out), .data_in(data_in_2), .q(basculed_4_q));
  or or_1 (or_1_out, and_3_out, and_7_out);
  and and_3 (and_3_out, a, basculed_3_q);
  or or_2 (or_2_out, and_4_out, and_8_out);
  and and_4 (and_4_out, a, basculed_4_q);
  and and_5 (data_out_1, not_2_out, or_1_out);
  and and_6 (data_out_2, not_2_out, or_2_out);
  and and_7 (and_7_out, not_1_out, basculed_1_q);
  and and_8 (and_8_out, not_1_out, basculed_2_q);
endmodule
