// Logisim project exercice8.2_v2.circ as structural Verilog
module BasculeRS (
  input  R,
  input  S,
  output Q
);

  wire nor_2_out;

  nor nor_1 (Q, R, nor_2_out);
  nor nor_2 (nor_2_out, Q, S);
endmodule

module BasculeD (
  input  D,
  input  data_in,
  output q
);

  wire and_1_out, and_2_out, nor_2_out, not_1_out;

  not not_1 (not_1_out, data_in);
  and and_1 (and_1_out, not_1_out, D);
  and and_2 (and_2_out, D, data_in);
  nor nor_1 (q, and_1_out, nor_2_out);
  nor nor_2 (nor_2_out, q, and_2_out);
endmodule

module Automate_x5 (
  input  horloge,
  input  n2,
  input  n1,
  input  n0,
  input  i,
  output out_6,
  output out_7,
  output out_8,
  output o
);

  wire and_1_out, and_2_out, and_4_out, and_5_out, and_6_out, and_8_out, and_9_out, and_10_out, and_11_out,
       and_12_out, and_14_out, basculed_1_q, basculed_2_q, basculed_3_q, basculed_4_q, not_1_out, not_2_out,
       not_3_out, not_4_out;

  BasculeD basculed_1 (.D(horloge), .data_in(n2), .q(basculed_1_q));
  BasculeD basculed_2 (.D(horloge), .data_in(n1), .q(basculed_2_q));
  BasculeD basculed_3 (.D(horloge), .data_in(n0), .q(basculed_3_q));
  BasculeD basculed_4 (.D(horloge), .data_in(i), .q(basculed_4_q));
  not not_1 (not_1_out, basculed_1_q);
  not not_2 (not_2_out, basculed_2_q);
  not not_3 (not_3_out, basculed_3_q);
  not not_4 (not_4_out, basculed_4_q);
  and and_1 (and_1_out, not_1_out, not_2_out, basculed_4_q);
  and and_2 (and_2_out, not_2_out, not_3_out, basculed_4_q);
  and and_3 (and_2_out, not_2_out, not_3_out, basculed_4_q);
  or or_1 (out_8, and_1_out, and_2_out, and_4_out);
  and and_4 (and_4_out, not_1_out, not_3_out, basculed_4_q);
  and and_5 (and_5_out, not_1_out, not_2_out, basculed_3_q);
  and and_6 (and_6_out, not_1_out, basculed_3_q, not_4_out);
  and and_7 (and_6_out, not_1_out, basculed_3_q, not_4_out);
  or or_2 (out_7, and_5_out, and_6_out, and_8_out);
  and and_8 (and_8_out, not_1_out, basculed_2_q, not_3_out, basculed_4_q);
  and and_9 (and_9_out, not_1_out, basculed_2_q, basculed_3_q, basculed_4_q);
  and and_10 (and_10_out, basculed_1_q, not_2_out, not_3_out, basculed_4_q);
  or or_3 (out_6, and_9_out, and_10_out);
  and and_11 (and_11_out, not_1_out, not_2_out, basculed_4_q);
  and and_12 (and_12_out, not_2_out, not_3_out, basculed_4_q);
  and and_13 (and_12_out, not_2_out, not_3_out, basculed_4_q);
  and and_14 (and_14_out, not_1_out, basculed_2_q, not_4_out);
  or or_4 (o, and_11_out, and_12_out, and_14_out);

  // Notes on the sheet:
  //   n2
  //   n1
  //   n0
  //   e2
  //   e1
  //   e0
endmodule

module Automate_mult5 (
  input  in_1,
  input  in_2,
  input  in_3,
  input  in_4,
  input  in_5,
  output out_6,
  output out_7,
  output out_8,
  output out_9
);

  wire and_1_out, and_2_out, and_4_out, and_5_out, and_7_out, and_8_out, and_10_out, and_11_out, and_13_out,
       and_14_out, and_15_out, and_16_out, and_18_out, and_20_out, and_21_out, basculed_1_q, basculed_2_q,
       basculed_3_q, basculed_4_q, not_1_out, not_2_out, not_3_out, not_4_out;

  BasculeD basculed_1 (.D(in_1), .data_in(in_2), .q(basculed_1_q));
  BasculeD basculed_2 (.D(in_1), .data_in(in_3), .q(basculed_2_q));
  BasculeD basculed_3 (.D(in_1), .data_in(in_4), .q(basculed_3_q));
  BasculeD basculed_4 (.D(in_1), .data_in(in_5), .q(basculed_4_q));
  not not_1 (not_1_out, basculed_1_q);
  not not_2 (not_2_out, basculed_2_q);
  not not_3 (not_3_out, basculed_3_q);
  not not_4 (not_4_out, basculed_4_q);
  and and_1 (and_1_out, not_1_out, not_2_out, not_3_out, basculed_4_q);
  and and_2 (and_2_out, not_1_out, not_2_out, basculed_3_q, basculed_4_q);
  and and_3 (and_2_out, not_1_out, not_2_out, basculed_3_q, basculed_4_q);
  or or_1 (out_8, and_1_out, and_2_out, and_4_out, and_5_out);
  and and_4 (and_4_out, not_1_out, basculed_2_q, not_3_out, basculed_4_q);
  and and_5 (and_5_out, basculed_1_q, not_2_out, not_3_out, not_4_out);
  and and_6 (and_5_out, basculed_1_q, not_2_out, not_3_out, not_4_out);
  and and_7 (and_7_out, not_1_out, not_2_out, basculed_3_q, not_4_out);
  and and_8 (and_8_out, not_1_out, not_2_out, basculed_3_q, basculed_4_q);
  and and_9 (and_8_out, not_1_out, not_2_out, basculed_3_q, basculed_4_q);
  and and_10 (and_10_out, not_1_out, basculed_2_q, not_3_out, basculed_4_q);
  or or_2 (out_7, and_7_out, and_8_out, and_10_out, and_11_out);
  and and_11 (and_11_out, not_1_out, basculed_2_q, basculed_3_q, not_4_out);
  and and_12 (and_11_out, not_1_out, basculed_2_q, basculed_3_q, not_4_out);
  and and_13 (and_13_out, not_1_out, basculed_2_q, basculed_3_q, basculed_4_q);
  and and_14 (and_14_out, basculed_1_q, not_2_out, not_3_out, basculed_4_q);
  or or_3 (out_6, and_13_out, and_14_out);
  and and_15 (and_15_out, not_1_out, not_2_out, not_3_out, basculed_4_q);
  and and_16 (and_16_out, not_1_out, not_2_out, basculed_3_q, basculed_4_q);
  and and_17 (and_16_out, not_1_out, not_2_out, basculed_3_q, basculed_4_q);
  and and_18 (and_18_out, not_1_out, basculed_2_q, not_3_out, not_4_out);
  and and_19 (and_18_out, not_1_out, basculed_2_q, not_3_out, not_4_out);
  or or_4 (out_9, and_15_out, and_16_out, and_18_out, and_20_out, and_21_out);
  and and_20 (and_20_out, not_1_out, basculed_2_q, basculed_3_q, not_4_out);
  and and_21 (and_21_out, basculed_1_q, not_2_out, not_3_out, basculed_4_q);
  and and_22 (and_21_out, basculed_1_q, not_2_out, not_3_out, basculed_4_q);

  // Notes on the sheet:
  //   n2
  //   n1
  //   n0
  //   e2
  //   e1
  //   e0
endmodule

module Automate_x5_v2 (
  input  in_1,
  input  in_2,
  output out_3
);

  wire and_1_out, and_2_out, and_4_out, and_5_out, and_7_out, and_8_out, and_9_out, and_10_out, and_12_out,
       basculed_1_q, basculed_2_q, basculed_3_q, basculed_4_q, basculed_5_q, basculed_6_q, basculed_7_q,
       not_1_out, not_2_out, not_3_out, not_4_out, not_5_out, or_1_out, or_2_out, or_3_out;

  not not_1 (not_1_out, in_1);
  BasculeD basculed_1 (.D(not_1_out), .data_in(or_3_out), .q(basculed_1_q));
  BasculeD basculed_2 (.D(not_1_out), .data_in(or_2_out), .q(basculed_2_q));
  BasculeD basculed_3 (.D(not_1_out), .data_in(or_1_out), .q(basculed_3_q));
  BasculeD basculed_4 (.D(in_1), .data_in(basculed_1_q), .q(basculed_4_q));
  BasculeD basculed_5 (.D(in_1), .data_in(basculed_2_q), .q(basculed_5_q));
  BasculeD basculed_6 (.D(in_1), .data_in(basculed_3_q), .q(basculed_6_q));
  BasculeD basculed_7 (.D(in_1), .data_in(in_2), .q(basculed_7_q));
  not not_2 (not_2_out, basculed_4_q);
  not not_3 (not_3_out, basculed_5_q);
  not not_4 (not_4_out, basculed_6_q);
  not not_5 (not_5_out, basculed_7_q);
  and and_1 (and_1_out, not_3_out, basculed_7_q);
  or or_1 (or_1_out, and_1_out, and_2_out);
  and and_2 (and_2_out, not_2_out, not_4_out, basculed_7_q);
  and and_3 (and_2_out, not_2_out, not_4_out, basculed_7_q);
  and and_4 (and_4_out, not_2_out, basculed_6_q, not_5_out);
  and and_5 (and_5_out, not_3_out, basculed_6_q);
  and and_6 (and_4_out, not_2_out, basculed_6_q, not_5_out);
  or or_2 (or_2_out, and_5_out, and_4_out, and_7_out);
  and and_7 (and_7_out, not_2_out, basculed_5_q, not_4_out, basculed_7_q);
  and and_8 (and_8_out, not_2_out, basculed_5_q, basculed_6_q, basculed_7_q);
  or or_3 (or_3_out, and_8_out, and_9_out);
  and and_9 (and_9_out, basculed_4_q, not_3_out, basculed_7_q);
  and and_10 (and_10_out, not_3_out, basculed_7_q);
  and and_11 (and_10_out, not_3_out, basculed_7_q);
  or or_4 (out_3, and_10_out, and_12_out);
  and and_12 (and_12_out, not_2_out, basculed_5_q, not_5_out);

  // Notes on the sheet:
  //   n2
  //   n1
  //   n0
  //   e2
  //   e1
  //   e0
  //   n2
  //   n1
  //   n0
  //   e2
  //   e1
  //   e0
endmodule
